# Fritzing sketch smartmqtttx (saved by Fritzing 0.9.3b)
breadboards: 1

parts:
  S1 = Pushbutton [package="[THT]"]
  U1 = ESP8266 WiFi Module [part_number=ESP8266]
  VCC1 = Battery
  R1 = Resistor [tolerance=±5% resistance=1k package="1206 [SMD]"]
  D1 = Rectifier Diode [package="Melf DO-213 AA [SMD]"]

nets:
  N1: S1.Pin_1, S1.Pin_2, D1.anode
  N2: S1.Pin_3, S1.Pin_4, U1.VCC, VCC1.+
  N3: U1.GPIO_2, R1.Pin_0
  N4: U1.CH_PD, R1.Pin_1, D1.cathode
  N5: U1.GND, VCC1.-

custom parts:
  ESP8266 WiFi Module: Generic WiFi Module based on the ESP8266 with onboard PCB antenna and UART communications
